# Fritzing sketch Secure_System_esp32 (saved by Fritzing 0.9.5d)
breadboards: 1

parts:
  U1 = LuaNode32 / ESP32 [part_number=ESP32S-PIN30]
  Part1 = sensor_biometrico
  Part2 = RFID-RC522-v2
  S1 = Pushbutton [package="[THT]"]
  S2 = Pushbutton [package="[THT]"]
  L1 = Solenoid
  KF-1 = KF-301 Relay [package=THT]
  PS1 = prefix0000 [part_number=S-350-60]

nets:
  N1: U1.D25, KF-1.signal
  GND: U1.GND, Part1.GND, Part2.GND, S1.Pin_1, S1.Pin_2, S2.Pin_1, S2.Pin_2, KF-1.ground
  N2: U1.Vin, KF-1.power
  3V3: U1.3V3, Part1.VCC, Part2.3.3V
  N3: U1.D15, S2.Pin_3, S2.Pin_4
  N4: U1.RX2, Part1.TX
  N5: U1.TX2, Part1.RX
  N6: U1.D5, S1.Pin_3, S1.Pin_4
  N7: U1.D18, Part2.SCK
  N8: U1.D19, Part2.MISO
  N9: U1.D21, Part2.SDA
  N10: U1.D22, Part2.RST
  N11: U1.D23, Part2.MOSI
  N12: L1.pin2, KF-1.NO
  N13: KF-1.C, PS1.connector0

custom parts:
  LuaNode32 / ESP32: New Image for LuaNode32 DOIT ESP32 DEVKIT V1. Base parts from LuaNode32 / ESP32 ESP32 based LuaNode32 by G.Noorlander DOIT Esp32 DevKit v1 (30 pins long, 11 pins width) by Werner Rothschopf (modified by vanepp Dec 2018)
  sensor_biometrico: Adafruit Optical Fingerprint Sensor
  RFID-RC522-v2: A simple China made RFID-RC522 Reader; do check the pin labels, as this is a MFRC522 based clone.
  KF-301 Relay: KF-301
